# Fritzing sketch rfid_1 (saved by Fritzing 0.9.5d)
breadboards: 2

parts:
  U3 = RFID RC522 SIP - 8 pins [chip_label="RFID RC522" package="SIP (Single Inline) [THT]"]
  Jetson_Nano1 = Jetson Nano
  R1 = Resistor [tolerance=±5% resistance=220 package="2010 [SMD]"]  # not connected

nets:
  N1: U3.NSS, Jetson_Nano1.3V3
  N2: U3.SCK, Jetson_Nano1.GPIO24
  N3: U3.MOSI, Jetson_Nano1.GPIO25
  N4: U3.MISO, Jetson_Nano1.GND
  N5: U3.RST, Jetson_Nano1.GPIO5

notes:
  spi 1
  23 clock white
  21 miso yellow
  19 mosi brown
  24 select0 green
  26 select1orange
  12 rest pink
  RFID 1
  spi 1
  23 clock white
  21 miso yellow
  19 mosi brown
  24 select0 green
  12 rest pink

custom parts:
  RFID RC522 SIP - 8 pins: A SIP stand-in part for RFID RC522 . With 8 pins on a 300 mil single inline package (SIP) footprint.
